# Fritzing sketch GRBL_EasyDriver (saved by Fritzing 0.6.5b)

parts:
  Z_Axis = EasyDriver_v44
  Arduino1 = Arduino
  Y_Axis = EasyDriver_v44
  X_Axis = EasyDriver_v44

nets:
  GND: Z_Axis.GND, Arduino1.GND, Y_Axis.GND, X_Axis.GND
  N1: Z_Axis.STEP, Arduino1.D4
  N2: Z_Axis.DIR, Arduino1.D7
  N3: Arduino1.D6, Y_Axis.DIR
  N4: Arduino1.D5, X_Axis.DIR
  N5: Arduino1.D3, Y_Axis.STEP
  N6: Arduino1.D2, X_Axis.STEP
